// Logisim project CPU_Sara_Teixeira_Cardoso21.circ as structural Verilog: 16 circuits, main circuit main
module main (
);

  wire clock_1_out, not_1_out, not_2_out, OvFlw_q, RST_out, uc_1_clk_ac, uc_1_clk_ir, uc_1_clk_pc,
       uc_1_clk_ram, \uc_1_direção , uc_1_load, uc_1_r_w_0, uc_1_reset_pc, ula_1_overflow, ula_1_zero, Zero_q;
  wire [2:0] uc_1_opcode;
  wire [3:0] ac_1_out_3, counter_1_q, mux_1_out_4, ram_1_data, \uc_1_endereço , uc_1_operando, ula_1_s;
  wire [7:0] ir_1_q, rom_1_data;

  not not_1 (not_1_out, uc_1_load);
  Counter #(.width(4), .max('hf), .trigger("falling")) counter_1 (
    .load(uc_1_load), .D(\uc_1_endereço ), .count(not_1_out), .Q(counter_1_q), .clk(uc_1_clk_pc),
    .clr(uc_1_reset_pc));  // open: carry
  UC uc_1 (
    .OPERANDO(uc_1_operando), .\Direção (\uc_1_direção ), .OPCODE(uc_1_opcode), .\INSTRUÇÃO (ir_1_q),
    .Clock(clock_1_out), .Clk_IR(uc_1_clk_ir), .Clk_PC(uc_1_clk_pc), .Clk_AC(uc_1_clk_ac),
    .Clk_Ram(uc_1_clk_ram), .Reset(RST_out), .Reset_PC(uc_1_reset_pc), .R_W_0(uc_1_r_w_0),
    .Overflow(OvFlw_q), .Zero(Zero_q), .Load(uc_1_load), .\Endereço (\uc_1_endereço ),
    .\Modo_de_Endereçamento (\uc_1_direção ));
  Clock clock_1 (.out(clock_1_out));
  Button RST (.out(RST_out));
  // Probe on rom_1_data
  IR ir_1 (.Clock(uc_1_clk_ir), .E(rom_1_data), .Q(ir_1_q));
  ROM #(.addrWidth(4)) rom_1 (.addr(counter_1_q), .data(rom_1_data));  // open: sel
  // Probe on ir_1_q
  // Probe on uc_1_opcode
  // Probe on uc_1_operando
  Mux mux_1 (.C(\uc_1_direção ), .A(uc_1_operando), .B(ram_1_data), .out_4(mux_1_out_4));
  // Probe on mux_1_out_4
  // Probe on ac_1_out_3
  ULA ula_1 (
    .D(\uc_1_direção ), .B(mux_1_out_4), .A(ac_1_out_3), .Overflow(ula_1_overflow), .\Operação (uc_1_opcode),
    .Zero(ula_1_zero), .S(ula_1_s));
  // Probe on ula_1_s
  AC ac_1 (.Clock(uc_1_clk_ac), .out_3(ac_1_out_3), .E(ula_1_s));
  D_Flip_Flop OvFlw (.clk(uc_1_clk_ac), .D(ula_1_overflow), .Q(OvFlw_q));  // open: Qn, preset, en, reset
  D_Flip_Flop Zero (.clk(uc_1_clk_ac), .D(ula_1_zero), .Q(Zero_q));  // open: Qn, preset, en, reset
  RAM #(.addrWidth(4), .dataWidth(4)) ram_1 (
    .addr(uc_1_operando), .data(ram_1_data), .clk(uc_1_clk_ram), .ld(uc_1_r_w_0));  // open: sel, clr
  Buffer buffer_1 (.C(not_2_out), .out_3(ram_1_data), .B(ac_1_out_3));
  not not_2 (not_2_out, uc_1_r_w_0);

  // Notes on the sheet:
  //   000
  //   0
  //   MOV
  //   000
  //   1
  //   MOV
  //   001
  //   2
  //   ADD
  //   001
  //   3
  //   ADD
  //   010
  //   SUB
  //   4
  //   010
  //   5
  //   SUB
  //   011
  //   6
  //   OR
  //   7
  //   OR
  //   011
  //   NOT
  //   8
  //   100
  //   100
  //   NOT
  //   9
  //   101
  //   A
  //   SHF
  //   SHF
  //   101
  //   B
  //   C
  //   110
  //   JPZ
  //   110
  //   JPO
  //   D
  //   111
  //   GO
  //   E
  //   STR
  //   F
  //   111
  //   Instruction Set
  //   0
  //   AC <= X
  //   1
  //   AC <= M(X)
  //   0
  //   AC <= AC+X
  //   1
  //   AC <= AC+M(X)
  //   0
  //   AC <= AC-X
  //   1
  //   AC <= AC-M(X)
  //   0
  //   AC <= AC OR X
  //   1
  //   AC <= AC OR M(X)
  //   0
  //   AC <= NOT X
  //   1
  //   AC <= NOT M( X)
  //   0
  //   AC <= AC << Q
  //   1
  //   AC <= AC >> Q
  //   0
  //   1
  //   PC <= X
  //   0
  //   M(X) <= AC 
  //   1
  //   PC <= X SE FLAG Z
  //   PC <= X SE FLAG O
  //   Memória de Programa
  //   PROCESSADOR RISC DE 4 BITS - ENGENHARIA DE COMPUTAÇÃO 2025-2
  //   Memória de Dados
endmodule

module Add_1 (
  input  A,
  input  B,
  input  Vem_1,
  output S,
  output Vai_1
);

  wire and_1_out, and_2_out, and_3_out, and_4_out, and_5_out, and_6_out, and_7_out, not_1_out, not_2_out,
       not_3_out, not_4_out, not_5_out, not_6_out;

  not not_1 (not_1_out, A);
  not not_2 (not_2_out, B);
  not not_3 (not_3_out, A);
  not not_4 (not_4_out, Vem_1);
  not not_5 (not_5_out, B);
  not not_6 (not_6_out, Vem_1);
  and and_1 (and_1_out, B, Vem_1);
  and and_2 (and_2_out, A, Vem_1);
  and and_3 (and_3_out, A, B);
  and and_4 (and_4_out, not_1_out, not_2_out, Vem_1);
  and and_5 (and_5_out, not_3_out, B, not_4_out);
  and and_6 (and_6_out, A, not_5_out, not_6_out);
  and and_7 (and_7_out, A, B, Vem_1);
  or or_1 (Vai_1, and_1_out, and_2_out, and_3_out);
  or or_2 (S, and_4_out, and_5_out, and_6_out, and_7_out);
endmodule

module Add_4 (
  input  [3:0] A,
  input  [3:0] B,
  output Overflow,
  output [3:0] S
);

  wire add_1_2_vai_1, add_1_3_vai_1, add_1_4_vai_1;

  // Probe on A
  Add_1 add_1_1 (.A(A[3]), .B(B[3]), .Vem_1(add_1_3_vai_1), .S(S[3]), .Vai_1(Overflow));
  Add_1 add_1_2 (.A(A[1]), .B(B[1]), .Vem_1(add_1_4_vai_1), .S(S[1]), .Vai_1(add_1_2_vai_1));
  Add_1 add_1_3 (.A(A[2]), .B(B[2]), .Vem_1(add_1_2_vai_1), .S(S[2]), .Vai_1(add_1_3_vai_1));
  // Probe on S
  Add_1 add_1_4 (.A(A[0]), .B(B[0]), .Vem_1(1'b0), .S(S[0]), .Vai_1(add_1_4_vai_1));
  // Probe on B
endmodule

module OR_4 (
  input  [3:0] B,
  input  [3:0] A,
  output [3:0] out_3
);

  or or_1 (out_3[3], A[3], B[3]);
  or or_2 (out_3[1], A[1], B[1]);
  or or_3 (out_3[2], A[2], B[2]);
  or or_4 (out_3[0], A[0], B[0]);
endmodule

module NOT_4 (
  input  [3:0] B,
  output [3:0] out_2
);

  not not_1 (out_2[3], B[3]);
  not not_2 (out_2[2], B[2]);
  not not_3 (out_2[0], B[0]);
  not not_4 (out_2[1], B[1]);
endmodule

module Buffer (
  input  [3:0] B,
  input  C,
  output [3:0] out_3
);

  assign out_3[3] = C ? B[3] : 1'bz;  // Controlled_Buffer controlled_buffer_1
  assign out_3[1] = C ? B[1] : 1'bz;  // Controlled_Buffer controlled_buffer_2
  assign out_3[2] = C ? B[2] : 1'bz;  // Controlled_Buffer controlled_buffer_3
  assign out_3[0] = C ? B[0] : 1'bz;  // Controlled_Buffer controlled_buffer_4
endmodule

module Dec3x8 (
  input  [2:0] \Operação ,
  output a,
  output b,
  output c,
  output d,
  output e,
  output f,
  output g,
  output h
);

  wire not_1_out, not_2_out, not_3_out, not_4_out, not_5_out, not_6_out, not_7_out, not_8_out, not_9_out,
       not_10_out, not_11_out, not_12_out;

  not not_1 (not_1_out, \Operação [2]);
  not not_2 (not_2_out, \Operação [1]);
  not not_3 (not_3_out, \Operação [0]);
  not not_4 (not_4_out, \Operação [2]);
  not not_5 (not_5_out, \Operação [1]);
  not not_6 (not_6_out, \Operação [2]);
  not not_7 (not_7_out, \Operação [0]);
  not not_8 (not_8_out, \Operação [2]);
  not not_9 (not_9_out, \Operação [1]);
  not not_10 (not_10_out, \Operação [0]);
  not not_11 (not_11_out, \Operação [1]);
  not not_12 (not_12_out, \Operação [0]);
  and and_1 (h, \Operação [2], \Operação [1], \Operação [0]);
  and and_2 (a, not_1_out, not_2_out, not_3_out);
  and and_3 (b, not_4_out, not_5_out, \Operação [0]);
  and and_4 (c, not_6_out, \Operação [1], not_7_out);
  and and_5 (d, not_8_out, \Operação [1], \Operação [0]);
  and and_6 (e, \Operação [2], not_9_out, not_10_out);
  and and_7 (f, \Operação [2], not_11_out, \Operação [0]);
  and and_8 (g, \Operação [2], \Operação [1], not_12_out);
endmodule

module Rot_esq (
  input  [3:0] abcd,
  input  [1:0] xy,
  output [3:0] ABCD_2
);

  wire and_1_out, and_2_out, and_3_out, and_4_out, and_5_out, and_6_out, and_7_out, and_8_out, and_9_out;

  and and_1 (and_1_out, ~xy[1], ~xy[0], abcd[3]);  // AND_Gate
  and and_2 (and_2_out, ~xy[1], xy[0], abcd[2]);  // AND_Gate
  and and_3 (and_3_out, xy[1], ~xy[0], abcd[1]);  // AND_Gate
  and and_4 (and_4_out, xy[1], xy[0], abcd[0]);
  and and_5 (and_5_out, ~xy[1], ~xy[0], abcd[2]);  // AND_Gate
  and and_6 (and_6_out, ~xy[1], xy[0], abcd[1]);  // AND_Gate
  and and_7 (and_7_out, xy[1], ~xy[0], abcd[0]);  // AND_Gate
  and and_8 (and_8_out, ~xy[1], ~xy[0], abcd[1]);  // AND_Gate
  and and_9 (and_9_out, ~xy[1], xy[0], abcd[0]);  // AND_Gate
  and and_10 (ABCD_2[0], ~xy[1], ~xy[0], abcd[0]);  // AND_Gate
  or or_1 (ABCD_2[3], and_1_out, and_2_out, and_3_out, and_4_out);
  or or_2 (ABCD_2[2], and_5_out, and_6_out, and_7_out);
  or or_3 (ABCD_2[1], and_8_out, and_9_out);
endmodule

module Rot_dir (
  input  [3:0] abcd,
  input  [1:0] xy,
  output [3:0] ABCD_2
);

  wire and_2_out, and_3_out, and_4_out, and_5_out, and_6_out, and_7_out, and_8_out, and_9_out, and_10_out;

  and and_1 (ABCD_2[3], ~xy[1], ~xy[0], abcd[3]);  // AND_Gate
  and and_2 (and_2_out, ~xy[1], ~xy[0], abcd[2]);  // AND_Gate
  or or_1 (ABCD_2[2], and_2_out, and_3_out);
  and and_3 (and_3_out, ~xy[1], xy[0], abcd[3]);  // AND_Gate
  and and_4 (and_4_out, ~xy[1], ~xy[0], abcd[1]);  // AND_Gate
  or or_2 (ABCD_2[1], and_4_out, and_5_out, and_6_out);
  and and_5 (and_5_out, ~xy[1], xy[0], abcd[2]);  // AND_Gate
  and and_6 (and_6_out, xy[1], ~xy[0], abcd[3]);  // AND_Gate
  and and_7 (and_7_out, ~xy[1], ~xy[0], abcd[0]);  // AND_Gate
  and and_8 (and_8_out, ~xy[1], xy[0], abcd[1]);  // AND_Gate
  or or_3 (ABCD_2[0], and_7_out, and_8_out, and_9_out, and_10_out);
  and and_9 (and_9_out, xy[1], ~xy[0], abcd[2]);  // AND_Gate
  and and_10 (and_10_out, xy[1], xy[0], abcd[3]);
endmodule

module Sub_1 (
  input  A,
  input  B,
  input  VEM1,
  output S,
  output VAI1
);

  wire and_1_out, and_2_out, and_3_out, and_4_out, and_5_out, and_6_out, and_7_out, not_1_out, not_2_out,
       not_3_out, not_4_out, not_5_out, not_6_out, not_7_out, not_8_out;

  not not_1 (not_1_out, A);
  not not_2 (not_2_out, B);
  not not_3 (not_3_out, A);
  not not_4 (not_4_out, VEM1);
  not not_5 (not_5_out, B);
  not not_6 (not_6_out, VEM1);
  not not_7 (not_7_out, A);
  not not_8 (not_8_out, A);
  and and_1 (and_1_out, not_1_out, not_2_out, VEM1);
  and and_2 (and_2_out, not_3_out, B, not_4_out);
  and and_3 (and_3_out, A, not_5_out, not_6_out);
  and and_4 (and_4_out, A, B, VEM1);
  and and_5 (and_5_out, not_7_out, VEM1);
  and and_6 (and_6_out, not_8_out, B);
  and and_7 (and_7_out, B, VEM1);
  or or_1 (S, and_1_out, and_2_out, and_3_out, and_4_out);
  or or_2 (VAI1, and_5_out, and_6_out, and_7_out);
endmodule

module sub_4 (
  input  [3:0] A,
  input  [3:0] B,
  output Overflow,
  output [3:0] S
);

  wire sub_1_2_vai1, sub_1_3_vai1, sub_1_4_vai1;

  // Probe on A
  Sub_1 sub_1_1 (.A(A[3]), .B(B[3]), .VEM1(sub_1_3_vai1), .S(S[3]), .VAI1(Overflow));
  Sub_1 sub_1_2 (.A(A[1]), .B(B[1]), .VEM1(sub_1_4_vai1), .S(S[1]), .VAI1(sub_1_2_vai1));
  Sub_1 sub_1_3 (.A(A[2]), .B(B[2]), .VEM1(sub_1_2_vai1), .S(S[2]), .VAI1(sub_1_3_vai1));
  // Probe on S
  Sub_1 sub_1_4 (.A(A[0]), .B(B[0]), .VEM1(1'b0), .S(S[0]), .VAI1(sub_1_4_vai1));
  // Probe on B
endmodule

module ULA (
  input  D,
  input  [3:0] B,
  input  [3:0] A,
  input  [2:0] \Operação ,
  output Overflow,
  output [3:0] S,
  output Zero
);

  wire add_4_1_overflow, and_1_out, and_2_out, dec3x8_1_a, dec3x8_1_b, dec3x8_1_c, dec3x8_1_d, dec3x8_1_e,
       dec3x8_1_f, dec3x8_1_g, dec3x8_1_h, not_1_out, sub_4_1_overflow;
  wire [3:0] add_4_1_s, buffer_6_out_3, not_4_1_out_2, or_4_1_out_3, rot_dir_1_abcd_2, rot_esq_1_abcd_2,
       sub_4_1_s;

  and and_1 (and_1_out, add_4_1_overflow, dec3x8_1_b);
  or or_1 (Overflow, and_1_out, and_2_out);
  and and_2 (and_2_out, sub_4_1_overflow, dec3x8_1_c);
  Dec3x8 dec3x8_1 (
    .\Operação (\Operação ), .a(dec3x8_1_a), .b(dec3x8_1_b), .c(dec3x8_1_c), .d(dec3x8_1_d), .e(dec3x8_1_e),
    .f(dec3x8_1_f), .g(dec3x8_1_g), .h(dec3x8_1_h));
  Buffer buffer_1 (.C(dec3x8_1_a), .out_3(S), .B(B));
  Add_4 add_4_1 (.Overflow(add_4_1_overflow), .S(add_4_1_s), .A(A), .B(B));
  Buffer buffer_2 (.C(dec3x8_1_b), .out_3(S), .B(add_4_1_s));
  and and_3 (Zero, ~S[0], ~S[1], ~S[2], ~S[3], ~dec3x8_1_g, ~dec3x8_1_h);  // AND_Gate
  sub_4 sub_4_1 (.Overflow(sub_4_1_overflow), .S(sub_4_1_s), .A(A), .B(B));
  Buffer buffer_3 (.C(dec3x8_1_c), .out_3(S), .B(sub_4_1_s));
  OR_4 or_4_1 (.B(B), .A(A), .out_3(or_4_1_out_3));
  Buffer buffer_4 (.C(dec3x8_1_d), .out_3(S), .B(or_4_1_out_3));
  NOT_4 not_4_1 (.out_2(not_4_1_out_2), .B(B));
  Buffer buffer_5 (.C(dec3x8_1_e), .out_3(S), .B(not_4_1_out_2));
  Rot_esq rot_esq_1 (.abcd(A), .ABCD_2(rot_esq_1_abcd_2), .xy(B[1:0]));
  Rot_dir rot_dir_1 (.ABCD_2(rot_dir_1_abcd_2), .abcd(A), .xy(B[1:0]));
  Buffer buffer_6 (.C(not_1_out), .out_3(buffer_6_out_3), .B(rot_esq_1_abcd_2));
  not not_1 (not_1_out, D);
  Buffer buffer_7 (.C(D), .out_3(buffer_6_out_3), .B(rot_dir_1_abcd_2));
  Buffer buffer_8 (.C(dec3x8_1_f), .out_3(S), .B(buffer_6_out_3));
endmodule

module AC (
  input  Clock,
  input  [3:0] E,
  output [3:0] out_3
);

  D_Flip_Flop D3 (.clk(Clock), .D(E[3]), .Q(out_3[3]));  // open: Qn, preset, en, reset
  D_Flip_Flop D2 (.clk(Clock), .D(E[2]), .Q(out_3[2]));  // open: Qn, preset, en, reset
  D_Flip_Flop D1 (.clk(Clock), .D(E[1]), .Q(out_3[1]));  // open: Qn, preset, en, reset
  D_Flip_Flop D0 (.clk(Clock), .D(E[0]), .Q(out_3[0]));  // open: Qn, preset, en, reset
endmodule

module Mux (
  input  [3:0] A,
  input  [3:0] B,
  input  C,
  output [3:0] out_4
);

  wire not_1_out;

  Buffer buffer_1 (.C(not_1_out), .out_3(out_4), .B(A));
  not not_1 (not_1_out, C);
  Buffer buffer_2 (.C(C), .out_3(out_4), .B(B));
endmodule

module IR (
  input  Clock,
  input  [7:0] E,
  output [7:0] Q
);

  D_Flip_Flop #(.trigger("falling")) D7 (.clk(Clock), .D(E[7]), .Q(Q[7]));  // open: Qn, preset, en, reset
  D_Flip_Flop #(.trigger("falling")) D6 (.clk(Clock), .D(E[6]), .Q(Q[6]));  // open: Qn, preset, en, reset
  D_Flip_Flop #(.trigger("falling")) D5 (.clk(Clock), .D(E[5]), .Q(Q[5]));  // open: Qn, preset, en, reset
  D_Flip_Flop #(.trigger("falling")) D4 (.clk(Clock), .D(E[4]), .Q(Q[4]));  // open: Qn, preset, en, reset
  D_Flip_Flop #(.trigger("falling")) D3 (.clk(Clock), .D(E[3]), .Q(Q[3]));  // open: Qn, preset, en, reset
  D_Flip_Flop #(.trigger("falling")) D2 (.clk(Clock), .D(E[2]), .Q(Q[2]));  // open: Qn, preset, en, reset
  D_Flip_Flop #(.trigger("falling")) D1 (.clk(Clock), .D(E[1]), .Q(Q[1]));  // open: Qn, preset, en, reset
  D_Flip_Flop #(.trigger("falling")) D0 (.clk(Clock), .D(E[0]), .Q(Q[0]));  // open: Qn, preset, en, reset
endmodule

module UC (
  input  [7:0] \INSTRUÇÃO ,
  input  Clock,
  input  Reset,
  input  Zero,
  input  Overflow,
  output Clk_IR,
  output Clk_AC,
  output [3:0] \Endereço ,
  output [3:0] OPERANDO,
  output Clk_Ram,
  output \Direção ,
  output Reset_PC,
  output Clk_PC,
  output [2:0] OPCODE,
  output R_W_0,
  output \Modo_de_Endereçamento ,
  output Load
);

  wire GOTO_out, JO_out, JZ_out, nand_1_out;
  wire [1:0] counter_1_q;

  Counter #(.width(2), .max('h3)) counter_1 (.Q(counter_1_q), .clk(Clock), .clr(Reset));  // open: load, D, count, carry
  and and_1 (Clk_PC, ~counter_1_q[1], counter_1_q[0]);  // AND_Gate
  and and_2 (Clk_AC, counter_1_q[1], ~counter_1_q[0]);  // AND_Gate
  and and_3 (Clk_IR, ~counter_1_q[1], ~counter_1_q[0]);  // AND_Gate
  and JO (JO_out, Overflow, Clk_PC, \INSTRUÇÃO [7], \INSTRUÇÃO [6], ~\INSTRUÇÃO [5], \INSTRUÇÃO [4]);  // AND_Gate
  and and_4 (Clk_Ram, counter_1_q[1], counter_1_q[0]);
  and JZ (JZ_out, Zero, Clk_PC, \INSTRUÇÃO [7], \INSTRUÇÃO [6], ~\INSTRUÇÃO [5], ~\INSTRUÇÃO [4]);  // AND_Gate
  and GOTO (GOTO_out, Clk_PC, \INSTRUÇÃO [7], \INSTRUÇÃO [6], \INSTRUÇÃO [5], ~\INSTRUÇÃO [4]);  // AND_Gate
  nand R_W (R_W_0, Clk_AC, \INSTRUÇÃO [7], \INSTRUÇÃO [6], \INSTRUÇÃO [5], \INSTRUÇÃO [4]);
  or or_1 (Load, GOTO_out, JZ_out, JO_out);
  nand nand_1 (nand_1_out, \INSTRUÇÃO [7], ~\INSTRUÇÃO [6], \INSTRUÇÃO [5], \INSTRUÇÃO [4]);  // NAND_Gate
  and and_5 (\Modo_de_Endereçamento , nand_1_out, \INSTRUÇÃO [4]);

  assign \Direção  = \INSTRUÇÃO [4];
  assign \Endereço  = \INSTRUÇÃO [3:0];
  assign OPCODE = \INSTRUÇÃO [7:5];
  assign OPERANDO = \INSTRUÇÃO [3:0];
  assign Reset_PC = Reset;
endmodule
