// Logisim project CPU_Sara_Teixeira_Cardoso4.circ as structural Verilog: 6 circuits, main circuit main
module main (
  input  [3:0] B,
  input  [3:0] A,
  input  in_3,
  input  in_4,
  input  in_5,
  input  in_6,
  output out_7,
  output [3:0] S
);

  wire [3:0] add_4_1_s, not_4_1_out_2, or_4_1_out_3;

  Buffer buffer_1 (.C(in_3), .out_3(S), .B(B));
  Add_4 add_4_1 (.Overflow(out_7), .S(add_4_1_s), .A(A), .B(B));
  Buffer buffer_2 (.C(in_4), .out_3(S), .B(add_4_1_s));
  OR_4 or_4_1 (.B(B), .A(A), .out_3(or_4_1_out_3));
  Buffer buffer_3 (.C(in_5), .out_3(S), .B(or_4_1_out_3));
  NOT_4 not_4_1 (.out_2(not_4_1_out_2), .B(B));
  Buffer buffer_4 (.C(in_6), .out_3(S), .B(not_4_1_out_2));
endmodule

module Add_1 (
  input  A,
  input  B,
  input  Vem_1,
  output S,
  output Vai_1
);

  wire and_1_out, and_2_out, and_3_out, and_4_out, and_5_out, and_6_out, and_7_out, not_1_out, not_2_out,
       not_3_out, not_4_out, not_5_out, not_6_out;

  not not_1 (not_1_out, A);
  not not_2 (not_2_out, B);
  not not_3 (not_3_out, A);
  not not_4 (not_4_out, Vem_1);
  not not_5 (not_5_out, B);
  not not_6 (not_6_out, Vem_1);
  and and_1 (and_1_out, B, Vem_1);
  and and_2 (and_2_out, A, Vem_1);
  and and_3 (and_3_out, A, B);
  and and_4 (and_4_out, not_1_out, not_2_out, Vem_1);
  and and_5 (and_5_out, not_3_out, B, not_4_out);
  and and_6 (and_6_out, A, not_5_out, not_6_out);
  and and_7 (and_7_out, A, B, Vem_1);
  or or_1 (Vai_1, and_1_out, and_2_out, and_3_out);
  or or_2 (S, and_4_out, and_5_out, and_6_out, and_7_out);
endmodule

module Add_4 (
  input  [3:0] A,
  input  [3:0] B,
  output Overflow,
  output [3:0] S
);

  wire add_1_2_vai_1, add_1_3_vai_1, add_1_4_vai_1;

  // Probe on A
  Add_1 add_1_1 (.A(A[3]), .B(B[3]), .Vem_1(add_1_3_vai_1), .S(S[3]), .Vai_1(Overflow));
  Add_1 add_1_2 (.A(A[1]), .B(B[1]), .Vem_1(add_1_4_vai_1), .S(S[1]), .Vai_1(add_1_2_vai_1));
  Add_1 add_1_3 (.A(A[2]), .B(B[2]), .Vem_1(add_1_2_vai_1), .S(S[2]), .Vai_1(add_1_3_vai_1));
  // Probe on S
  Add_1 add_1_4 (.A(A[0]), .B(B[0]), .Vem_1(1'b0), .S(S[0]), .Vai_1(add_1_4_vai_1));
  // Probe on B
endmodule

module OR_4 (
  input  [3:0] B,
  input  [3:0] A,
  output [3:0] out_3
);

  or or_1 (out_3[3], A[3], B[3]);
  or or_2 (out_3[2], A[2], B[2]);
  or or_3 (out_3[1], A[1], B[1]);
  or or_4 (out_3[0], A[0], B[0]);
endmodule

module NOT_4 (
  input  [3:0] B,
  output [3:0] out_2
);

  not not_1 (out_2[2], B[2]);
  not not_2 (out_2[3], B[3]);
  not not_3 (out_2[0], B[0]);
  not not_4 (out_2[1], B[1]);
endmodule

module Buffer (
  input  [3:0] B,
  input  C,
  output [3:0] out_3
);

  assign out_3[3] = C ? B[3] : 1'bz;  // Controlled_Buffer controlled_buffer_1
  assign out_3[1] = C ? B[1] : 1'bz;  // Controlled_Buffer controlled_buffer_2
  assign out_3[2] = C ? B[2] : 1'bz;  // Controlled_Buffer controlled_buffer_3
  assign out_3[0] = C ? B[0] : 1'bz;  // Controlled_Buffer controlled_buffer_4
endmodule
